// Logisim project COMP.circ as structural Verilog: 1 circuit, main circuit main
module main (
  input  FGI,
  input  FGO,
  input  [7:0] INPR,
  output R,
  output out_5,
  output [2:0] out_6,
  output [11:0] out_7,
  output IEN
);

  wire and_1_out, and_2_out, d_ff_1_q, d_ff_2_q, decoder_1_out0, decoder_1_out1, decoder_1_out2,
       decoder_1_out3, decoder_1_out4, decoder_1_out5, decoder_1_out6, decoder_1_out7, main_1_p1, main_1_p2,
       main_1_p3, main_1_p4, main_1_p5, main_1_p6, main_1_p7, main_1_p8, main_1_p9, main_3_p21, main_3_p22,
       main_6_p1, main_12_ac15, main_12_e_2, main_12_fgi_2, main_12_fgo_2, main_13_p41, main_13_p42,
       main_13_p50, main_13_p51, main_13_p57, main_13_p67, main_13_p68, main_13_p69, not_1_out, not_2_out;
  wire [1:0] main_13_p46, main_13_p48, main_13_p52, main_13_p65;
  wire [2:0] main_13_p38, main_13_p43, main_13_p54;
  wire [6:0] main_13_p58;
  wire [11:0] main_13_p26;
  wire [20:0] main_13_p5;

  // counter_main main_1: pin names not known; wires that end beside it: main_1_p1, main_1_p2, main_1_p3, main_1_p4, main_1_p5, main_1_p6, main_1_p7, main_1_p8, main_1_p9
  Decoder #(.select(3)) decoder_1 (
    .out0(decoder_1_out0), .out1(decoder_1_out1), .out2(decoder_1_out2), .out3(decoder_1_out3),
    .out4(decoder_1_out4), .out5(decoder_1_out5), .out6(decoder_1_out6), .out7(decoder_1_out7), .sel(out_6));  // open: en
  not not_1 (not_1_out, out_5);
  and and_1 (and_1_out, decoder_1_out7, not_1_out, main_1_p5);
  and and_2 (and_2_out, decoder_1_out7, out_5, main_1_p5);
  // Register_Ref_main main_2: pin names not known; wires that end beside it: and_1_out, out_7
  // Memory_Ref_main main_3: pin names not known; wires that end beside it: main_1_p2, main_1_p3, main_1_p4, main_1_p5, main_1_p6, main_1_p7, main_1_p8, main_1_p9, decoder_1_out0, decoder_1_out1, decoder_1_out2, decoder_1_out3, decoder_1_out4, decoder_1_out5, decoder_1_out6, decoder_1_out7, R, IEN, FGI, FGO, main_3_p21, main_3_p22, out_5
  // Input_Output_Ref_main main_4: pin names not known; wires that end beside it: and_2_out, out_7
  // ALU_main main_5: pin names not known; wires that end beside it: INPR
  // memory_main main_6: pin names not known; wires that end beside it: main_6_p1
  // IncReg12_main main_7: pin names not known
  // IncReg12_main main_8: pin names not known
  // IncReg16_main main_9: pin names not known
  // IR_main main_10: pin names not known
  // IncReg16_main main_11: pin names not known
  D_Flip_Flop d_ff_1 (.D(FGO), .Q(d_ff_1_q));  // open: clk, Qn, preset, en, reset
  D_Flip_Flop d_ff_2 (.D(FGI), .Q(d_ff_2_q));  // open: clk, Qn, preset, en, reset
  val_extract1_main main_12 (
    .E(main_3_p22), .FGO(d_ff_1_q), .FGI(d_ff_2_q), .AC15(main_12_ac15), .E_2(main_12_e_2),
    .FGO_2(main_12_fgo_2), .FGI_2(main_12_fgi_2));  // open: DR, AC, AC_Val, DR_Val
  // MAINLOGIC_main main_13: pin names not known; wires that end beside it: main_12_ac15, main_12_e_2, main_12_fgo_2, main_12_fgi_2, main_13_p5[0], main_13_p5[1], main_13_p5[2], main_13_p5[3], main_13_p5[4], main_13_p5[5], main_13_p5[6], main_13_p5[7], main_13_p5[8], main_13_p5[9], main_13_p5[10], main_13_p5[11], main_13_p5[12], main_13_p5[13], main_13_p5[14], main_13_p5[15], main_13_p5[16], main_13_p5[17], main_13_p5[18], main_13_p5[19], main_13_p5[20], main_13_p26[0], main_13_p26[1], main_13_p26[2], main_13_p26[3], main_13_p26[4], main_13_p26[5], main_13_p26[6], main_13_p26[7], main_13_p26[8], main_13_p26[9], main_13_p26[10], main_13_p26[11], main_13_p38[0], main_13_p38[1], main_13_p38[2], main_13_p41, main_13_p42, main_13_p43[0], main_13_p43[1], main_13_p43[2], main_13_p46[0], main_13_p46[1], main_13_p48[0], main_13_p48[1], main_13_p50, main_13_p51, main_13_p52[0], main_13_p52[1], main_13_p54[0], main_13_p54[1], main_13_p54[2], main_13_p57, main_13_p58[0], main_13_p58[1], main_13_p58[2], main_13_p58[3], main_13_p58[4], main_13_p58[5], main_13_p58[6], main_13_p65[0], main_13_p65[1], main_13_p67, main_13_p68, main_13_p69, main_13_p50, main_13_p51
  not not_2 (not_2_out, main_13_p67);
  J_K_Flip_Flop R_FLAG (.J(main_13_p41), .K(main_13_p42), .Q(R));  // open: clk, Qn, preset, en, reset
  D_Flip_Flop S (.D(main_13_p57), .Q(main_3_p21));  // open: clk, Qn, preset, en, reset
  J_K_Flip_Flop SC (.J(main_13_p67), .K(not_2_out), .Q(main_1_p1));  // open: clk, Qn, preset, en, reset
  J_K_Flip_Flop IEN_FLAG (.J(main_13_p69), .K(main_13_p68), .Q(IEN));  // open: clk, Qn, preset, en, reset

  // Notes on the sheet:
  //   RAM 7
  //           AR 1
  //   PC 2
  //   DR 3
  //   IR 5
  //   TR 6
endmodule
